# Fritzing sketch blinka-diod (saved by Fritzing 0.9.4)
breadboards: 1

parts:
  Part1 = Arduino Uno (Rev3)
  LED1 = smd LED [color="Red (633nm)" package="0805 [SMD]"]
  R3 = Resistor [tolerance=±5% resistance=220 package=THT]

nets:
  N1: Part1.D2, LED1.anode
  N2: Part1.GND, R3.Pin_0
  N3: LED1.cathode, R3.Pin_1
