# Fritzing sketch motor-bil-sensor (saved by Fritzing 0.9.4)
breadboards: 1

parts:
  Part1 = Arduino Uno (Rev3) - ICSP
  L298N1 = L298N DC motor driver
  M1 = DC Motor  # not connected
  M2 = DC Motor  # not connected
  HC-SR04_Sensor_1 = HC-SR04 Ultrasonic Distance Sensor

nets:
  N1: Part1.D8, HC-SR04_Sensor_1.ECHO
  N2: Part1.D9_PWM, L298N1.ENB
  N3: Part1.D11_PWM/MOSI, L298N1.IN3
  N4: Part1.D12/MISO, L298N1.IN2
  N5: Part1.D13/SCK, L298N1.IN1
  N6: Part1.D6_PWM, L298N1.ENA
  N7: Part1.D7, HC-SR04_Sensor_1.TRIG
  5V: Part1.5V, L298N1.5V, HC-SR04_Sensor_1.VCC
  GND: Part1.GND, L298N1.GND, HC-SR04_Sensor_1.GND

custom parts:
  L298N DC motor driver: 2x DC motor driver with 78M05 positive voltage regulator (7..35 V) L298N: max 46 V, 2 A Set 5 V Enable jumper to enable 5 V regultor (needed for the L298N) and +5 V output at screw terminal or supply external +5 V at screw terminal Set ENA and/or ENB to +5 V to enable motor permanently or supply ENA and/or ENB with PWM signal IN1 and IN2 set rotation directory for motor A (OUT1/OUT2) IN2 and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
